// Logisim project mips.circ as structural Verilog: 6 circuits, main circuit main
module main (
  input  in_1
);

  wire ALUSrc, and_1_out, Branch, ClockMain, Jump, L2, MemRead, MemToReg, MemWrite, not_1_out, or_1_out,
       RegDst, RegWrite;
  wire [1:0] ALUOp;
  wire [2:0] multiplexer_1_out, opcode, rs, rt, ULACtrl;
  wire [2:2] rd;
  wire [7:0] adder_1_out, adress_Imm, banco_de_registradores_parte_2_1_read_data_1, L1, multiplexer_3_out,
       PC_q, ram_1_data, Retorno, rt_Saida;

  Clock clock_1 (.out(ClockMain));
  Register PC (.D(Retorno), .Q(PC_q), .clk(ClockMain), .clr(in_1));  // open: en
  Adder adder_1 (.a(8'h1), .b(PC_q), .out(adder_1_out));  // open: cin, cout
  ROM #(.dataWidth(18)) rom_1 (.addr(PC_q), .data({opcode, rs, rt, rd[2], adress_Imm}));  // open: sel
  Unidade_de_controle___Parte_4 unidade_de_controle_parte_4_1 (
    .opcode(opcode), .RegDst(RegDst), .RegWrite(RegWrite), .ALUSrc(ALUSrc), .MemWrite(MemWrite),
    .MemRead(MemRead), .MemToReg(MemToReg), .Branch(Branch), .Jump(Jump), .ALUOp(ALUOp));
  and and_1 (and_1_out, Branch, L2);
  or or_1 (or_1_out, Jump, and_1_out);
  Multiplexer #(.width(3), .enable("false")) multiplexer_1 (
    .in0(rt), .in1({rd[2], adress_Imm[7:6]}), .out(multiplexer_1_out), .sel(RegDst));
  Multiplexer #(.width(8), .enable("false")) multiplexer_2 (
    .in0(adder_1_out), .in1(adress_Imm), .out(Retorno), .sel(or_1_out));
  Banco_de_registradores___Parte_2 banco_de_registradores_parte_2_1 (
    .Read1(rs), .Read2(rt), .WriterResgister(multiplexer_1_out), .Reg_Writer(RegWrite), .Clock(ClockMain),
    .Clear(in_1), .Read_data_1(banco_de_registradores_parte_2_1_read_data_1), .Read_data_2(rt_Saida));  // open: Writer_Data
  Controle_ULA___Parte_4 controle_ula_parte_4_1 (.funct(adress_Imm[2:0]), .ALUOp(ALUOp), .ULACtrl(ULACtrl));
  RAM #(.bus("separate")) ram_1 (
    .addr(L1), .din(rt_Saida), .data(ram_1_data), .str(MemWrite), .clk(not_1_out), .ld(MemRead), .clr(in_1));  // open: sel
  not not_1 (not_1_out, ClockMain);
  Multiplexer #(.width(8), .enable("false")) multiplexer_3 (
    .in0(rt_Saida), .in1(adress_Imm), .out(multiplexer_3_out), .sel(ALUSrc));
  Multiplexer #(.width(8), .enable("false")) multiplexer_4 (.in0(ram_1_data), .in1(L1), .sel(MemToReg));  // open: out
  ULA___Parte_3 ula_parte_3_1 (
    .Entrada_A(banco_de_registradores_parte_2_1_read_data_1), .\Entrada_Função (ULACtrl),
    .Entrada_B(multiplexer_3_out), .Shamt(adress_Imm[5:3]), .R(L1), .Igual(L2));

  // Other names for the same wires on the sheet: ClearMain = in_1; funct[2:0] = adress_Imm[2:0];
  //   rd[1:0] = adress_Imm[7:6]; shamt[2:0] = adress_Imm[5:3]
endmodule

module Contador_PC___Parte_1 (
  input  in_1,
  output [7:0] out_2
);

  wire clock_1_out;
  wire [7:0] adder_1_out, PC_q;

  Register PC (.D(adder_1_out), .Q(PC_q), .clk(clock_1_out), .clr(in_1));  // open: en
  Clock clock_1 (.out(clock_1_out));
  Adder adder_1 (.a(8'h1), .b(PC_q), .out(adder_1_out));  // open: cin, cout
  ROM rom_1 (.addr(PC_q), .data(out_2));  // open: sel
endmodule

module Banco_de_registradores___Parte_2 (
  input  [2:0] Read1,
  input  [2:0] Read2,
  input  [7:0] Writer_Data,
  input  [2:0] WriterResgister,
  input  Reg_Writer,
  input  Clock,
  input  Clear,
  output [7:0] Read_data_1,
  output [7:0] Read_data_2
);

  wire WE0, WE1, WE2, WE3, WE4, WE5, WE6, WE7;
  wire [7:0] demultiplexer_2_out0, demultiplexer_2_out1, demultiplexer_2_out2, demultiplexer_2_out3,
       demultiplexer_2_out4, demultiplexer_2_out5, demultiplexer_2_out6, demultiplexer_2_out7, Reg0, Reg1,
       Reg2, Reg3, Reg4, Reg5, Reg6, Reg7;

  Demultiplexer #(.select(3), .enable("false")) demultiplexer_1 (
    .out0(WE0), .out1(WE1), .out2(WE2), .out3(WE3), .out4(WE4), .out5(WE5), .out6(WE6), .out7(WE7),
    .in(Reg_Writer), .sel(WriterResgister));
  Demultiplexer #(.select(3), .width(8), .enable("false")) demultiplexer_2 (
    .out0(demultiplexer_2_out0), .out1(demultiplexer_2_out1), .out2(demultiplexer_2_out2),
    .out3(demultiplexer_2_out3), .out4(demultiplexer_2_out4), .out5(demultiplexer_2_out5),
    .out6(demultiplexer_2_out6), .out7(demultiplexer_2_out7), .in(Writer_Data), .sel(WriterResgister));
  Register u_Reg0 (.D(demultiplexer_2_out0), .en(WE0), .Q(Reg0), .clk(Clock), .clr(Clear));
  Register u_Reg1 (.D(demultiplexer_2_out1), .en(WE1), .Q(Reg1), .clk(Clock), .clr(Clear));
  Register u_Reg2 (.D(demultiplexer_2_out2), .en(WE2), .Q(Reg2), .clk(Clock), .clr(Clear));
  Register u_Reg3 (.D(demultiplexer_2_out3), .en(WE3), .Q(Reg3), .clk(Clock), .clr(Clear));
  Register u_Reg4 (.D(demultiplexer_2_out4), .en(WE4), .Q(Reg4), .clk(Clock), .clr(Clear));
  Register u_Reg5 (.D(demultiplexer_2_out5), .en(WE5), .Q(Reg5), .clk(Clock), .clr(Clear));
  Register u_Reg6 (.D(demultiplexer_2_out6), .en(WE6), .Q(Reg6), .clk(Clock), .clr(Clear));
  Register u_Reg7 (.D(demultiplexer_2_out7), .en(WE7), .Q(Reg7), .clk(Clock), .clr(Clear));
  Multiplexer #(.select(3), .width(8), .enable("false")) multiplexer_1 (
    .in0(Reg0), .in1(Reg1), .in2(Reg2), .in3(Reg3), .in4(Reg4), .in5(Reg5), .in6(Reg6), .in7(Reg7),
    .out(Read_data_1), .sel(Read1));
  Multiplexer #(.select(3), .width(8), .enable("false")) multiplexer_2 (
    .in0(Reg0), .in1(Reg1), .in2(Reg2), .in3(Reg3), .in4(Reg4), .in5(Reg5), .in6(Reg6), .in7(Reg7),
    .out(Read_data_2), .sel(Read2));

  // Other names for the same wires on the sheet: Clock0 = Clock; Clock1 = Clock; Clock2 = Clock; Clock3 = Clock;
  //   Clock4 = Clock; Clock5 = Clock; Clock6 = Clock; Clock7 = Clock; R1[2:0] = Read1; R2[2:0] = Read2

  // Notes on the sheet:
  //   Registradores
endmodule

module ULA___Parte_3 (
  input  [7:0] Entrada_A,
  input  [2:0] \Entrada_Função ,
  input  [7:0] Entrada_B,
  input  [2:0] Shamt,
  output [7:0] R,
  output Igual
);

  wire comparator_1_lt;
  wire [7:0] AComp, adder_1_out, ADiv, AMult, ANeg, AShiftDir, AShiftEsq, ASoma, ASub, BComp, BDiv,
       bit_extender_1_out, BMult, BSoma, BSub, divider_1_out, multiplier_1_out, negator_1_out, shifter_1_out,
       shifter_2_out, subtractor_1_out;

  Demultiplexer #(.select(3), .width(8), .enable("false")) demultiplexer_1 (
    .out0(ASoma), .out1(ASub), .out2(AMult), .out3(ADiv), .out4(ANeg), .out5(AComp), .out6(AShiftEsq),
    .out7(AShiftDir), .in(Entrada_A), .sel(\Entrada_Função ));
  Demultiplexer #(.select(3), .width(8), .enable("false")) demultiplexer_2 (
    .out0(BSoma), .out1(BSub), .out2(BMult), .out3(BDiv), .out5(BComp), .in(Entrada_B), .sel(\Entrada_Função ));  // open: out4, out6, out7
  Adder adder_1 (.a(ASoma), .b(BSoma), .out(adder_1_out));  // open: cin, cout
  Subtractor subtractor_1 (.a(ASub), .b(BSub), .out(subtractor_1_out));  // open: bin, bout
  Multiplier multiplier_1 (.a(AMult), .b(BMult), .out(multiplier_1_out));  // open: cin, cout
  Divider divider_1 (.a(ADiv), .b(BDiv), .out(divider_1_out));  // open: upper, rem
  Negator negator_1 (.in(ANeg), .out(negator_1_out));
  Comparator comparator_1 (.a(AComp), .b(BComp), .eq(Igual), .lt(comparator_1_lt));  // open: gt
  Shifter shifter_1 (.in(AShiftEsq), .\dist (Shamt), .out(shifter_1_out));
  Shifter #(.shift("lr")) shifter_2 (.in(AShiftDir), .\dist (Shamt), .out(shifter_2_out));
  assign bit_extender_1_out = {{7{1'b0}}, comparator_1_lt};  // Bit_Extender bit_extender_1
  Multiplexer #(.select(3), .width(8), .enable("false")) multiplexer_1 (
    .in0(adder_1_out), .in1(subtractor_1_out), .in2(multiplier_1_out), .in3(divider_1_out),
    .in4(negator_1_out), .in5(bit_extender_1_out), .in6(shifter_1_out), .in7(shifter_2_out), .out(R),
    .sel(\Entrada_Função ));

  // Other names for the same wires on the sheet: ShantDir[2:0] = Shamt; ShantEsq[2:0] = Shamt
endmodule

module Unidade_de_controle___Parte_4 (
  input  [2:0] opcode,
  output RegDst,
  output RegWrite,
  output ALUSrc,
  output MemWrite,
  output MemRead,
  output MemToReg,
  output Branch,
  output Jump,
  output [1:0] ALUOp
);

  wire and_1_out, and_4_out, and_5_out, and_8_out, and_9_out, nor_2_out;

  nor nor_1 (RegDst, opcode[0], opcode[1], opcode[2]);
  nor nor_2 (nor_2_out, opcode[1], opcode[2]);
  and and_1 (and_1_out, ~opcode[0], ~opcode[1], opcode[2]);  // AND_Gate
  ExactlyOne xor_1 (.out(ALUSrc), .in0(opcode[0]), .in1(opcode[1]), .in2(opcode[2]));
  and and_2 (MemWrite, ~opcode[0], opcode[1], ~opcode[2]);  // AND_Gate
  and and_3 (MemRead, opcode[0], ~opcode[1], ~opcode[2]);  // AND_Gate
  and and_4 (and_4_out, ~opcode[0], ~opcode[1], ~opcode[2]);  // AND_Gate
  and and_5 (and_5_out, ~opcode[0], ~opcode[1], opcode[2]);  // AND_Gate
  and and_6 (Branch, opcode[0], opcode[1], ~opcode[2]);  // AND_Gate
  and and_7 (Jump, opcode[0], opcode[1], opcode[2]);
  and and_8 (and_8_out, opcode[0], opcode[1], ~opcode[2]);  // AND_Gate
  and and_9 (and_9_out, ~opcode[0], ~opcode[1], opcode[2]);  // AND_Gate
  and and_10 (ALUOp[1], ~opcode[0], ~opcode[1]);  // AND_Gate
  or or_1 (RegWrite, nor_2_out, and_1_out);
  or or_2 (MemToReg, and_4_out, and_5_out);
  or or_3 (ALUOp[0], and_8_out, and_9_out);
endmodule

module Controle_ULA___Parte_4 (
  input  [2:0] funct,
  input  [1:0] ALUOp,
  output [2:0] ULACtrl
);

  Multiplexer #(.select(2), .width(3), .enable("false")) multiplexer_1 (
    .in0(3'b000), .in1(3'b101), .in2(funct), .in3(3'b000), .out(ULACtrl), .sel(ALUOp));
endmodule
